# Fritzing sketch raspberrypisecurity (saved by Fritzing 0.9.3b)

parts:
  Raspberry_Pi_1 = Raspberry Pi 3 [part_number=RPI-3-V1.2]
  PIR1 = PIR sensor
  J1 = Piezo Speaker
  Keypad4x2 = Keypad Membran 4x4

nets:
  N1: Raspberry_Pi_1.GIPO4, PIR1.SIG
  N2: Raspberry_Pi_1.GIPO17, J1.pin2
  N3: Raspberry_Pi_1.GIPO6, Keypad4x2.Pin4
  N4: Raspberry_Pi_1.GIPO13, Keypad4x2.Pin3
  N5: Raspberry_Pi_1.GIPO19, Keypad4x2.Pin2
  N6: Raspberry_Pi_1.GIPO26, Keypad4x2.Pin1
  N7: Raspberry_Pi_1.GIPO21, Keypad4x2.Pin5
  N8: Raspberry_Pi_1.GIPO20, Keypad4x2.Pin6
  N9: Raspberry_Pi_1.GIPO16, Keypad4x2.Pin7
  N10: Raspberry_Pi_1.GIPO12, Keypad4x2.Pin8
  GND: Raspberry_Pi_1.GND, PIR1.GND, J1.pin1
  5V: Raspberry_Pi_1.5V, PIR1.VDD

custom parts:
  Keypad Membran 4x4: Membrane Keypad 4x4 Matrix
